# Fritzing sketch fritzing (saved by Fritzing 0.9.3b)
breadboards: 1

parts:
  Antenna = HC-12 Antenna
  LED = LEDs [package=led10mm]
  LED_2 = Resistor [tolerance=±5% resistance=220 package=THT]
  For_LCD = Resistor [tolerance=±5% resistance=220 package=THT]
  Arduino_Uno = Arduino Uno (Rev3) - ICSP
  LCD = LCD-16X2 [package=lcd-16x2]
  Buzzer = Piezo Speaker
  Key = Resistor [tolerance=±5% resistance=10k package="0402 [SMD]"]
  Key_2 = Pushbutton [package="[SMD]"]
  HC-12 = HC-12 Module
  Clear = Resistor [tolerance=±5% resistance=10k package="0402 [SMD]"]
  Clear_2 = Pushbutton [package="[SMD]"]
  Setting = Resistor [tolerance=±5% resistance=10k package="0402 [SMD]"]
  Setting_2 = Pushbutton [package="[SMD]"]

nets:
  N1: Antenna.ANT, HC-12.ANT
  N2: LED.C, LED_2.Pin_0
  N3: LED.A, Arduino_Uno.D2
  GND: LED_2.Pin_1, Arduino_Uno.GND, LCD.VSS, LCD.VO, LCD.R_W, LCD.K, Buzzer.pin2, Key.Pin_0, HC-12.GND, Clear.Pin_0, Setting.Pin_0
  5V: For_LCD.Pin_0, Arduino_Uno.5V, LCD.VDD, Key_2.Pin_3, Key_2.Pin_4, HC-12.VCC, Clear_2.Pin_3, Clear_2.Pin_4, Setting_2.Pin_3
  N4: For_LCD.Pin_1, LCD.A
  N5: Arduino_Uno.D8, LCD.DB5
  N6: Arduino_Uno.D9_PWM, LCD.DB6
  N7: Arduino_Uno.D10_PWM/SS, HC-12.TXD
  N8: Arduino_Uno.D11_PWM/MOSI, HC-12.RXD
  N9: Arduino_Uno.D12/MISO, LCD.DB7
  N10: Arduino_Uno.D13/SCK, Clear.Pin_1, Clear_2.Pin_1, Clear_2.Pin_2
  N11: Arduino_Uno.D0/RX, LCD.RS
  N12: Arduino_Uno.D1/TX, LCD.E
  N13: Arduino_Uno.D3_PWM, Key.Pin_1, Key_2.Pin_1, Key_2.Pin_2
  N14: Arduino_Uno.D5_PWM, Buzzer.pin1
  N15: Arduino_Uno.D6_PWM, Setting.Pin_1, Setting_2.Pin_1, Setting_2.Pin_2
  N16: Arduino_Uno.D7, LCD.DB4

custom parts:
  HC-12 Antenna: Antenna for HC-12 433Mhz Module
  HC-12 Module: HC-12 433Mhz Module
