# Fritzing sketch fritzing_new (saved by Fritzing 0.9.3b)
breadboards: 1

parts:
  Antenna = HC-12 Antenna
  LED = LEDs [package=led10mm]
  LED_2 = Resistor [tolerance=±5% resistance=220 package=THT]
  For_LCD = Resistor [tolerance=±5% resistance=220 package=THT]
  Arduino_Uno = Arduino Uno (Rev3) - ICSP
  LCD = LCD-16X2 [package=lcd-16x2]
  Buzzer = Piezo Speaker
  Key = Resistor [tolerance=±5% resistance=10k package="0402 [SMD]"]
  Key_2 = Pushbutton [package="[SMD]"]
  HC-12 = HC-12 Module
  Edit = Pushbutton [package="[SMD]"]
  Setting = Resistor [tolerance=±5% resistance=10k package="0402 [SMD]"]
  Edit_2 = Resistor [tolerance=±5% resistance=10k package="0402 [SMD]"]
  Setting_2 = Pushbutton [package="[SMD]"]

nets:
  N1: Antenna.ANT, HC-12.ANT
  N2: LED.C, LED_2.Pin_0
  N3: LED.A, Arduino_Uno.D2
  GND: LED_2.Pin_1, Arduino_Uno.GND, LCD.VSS, LCD.VO, LCD.R_W, LCD.K, Buzzer.pin1, Key.Pin_0, HC-12.GND, Setting.Pin_0, Edit_2.Pin_0
  5V: For_LCD.Pin_0, Arduino_Uno.5V, LCD.VDD, Key_2.Pin_3, Key_2.Pin_4, HC-12.VCC, Edit.Pin_3, Edit.Pin_4, Setting_2.Pin_3, Setting_2.Pin_4
  N4: For_LCD.Pin_1, LCD.A
  N5: Arduino_Uno.A5/SCL, Setting.Pin_1, Setting_2.Pin_1, Setting_2.Pin_2
  N6: Arduino_Uno.D8, LCD.DB5
  N7: Arduino_Uno.D9_PWM, LCD.DB6
  N8: Arduino_Uno.D10_PWM/SS, HC-12.TXD
  N9: Arduino_Uno.D11_PWM/MOSI, HC-12.RXD
  N10: Arduino_Uno.D12/MISO, LCD.DB7
  N11: Arduino_Uno.D13/SCK, Edit.Pin_1, Edit.Pin_2, Edit_2.Pin_1
  N12: Arduino_Uno.D3_PWM, LCD.RS
  N13: Arduino_Uno.D4, Key.Pin_1, Key_2.Pin_1, Key_2.Pin_2
  N14: Arduino_Uno.D5_PWM, LCD.E
  N15: Arduino_Uno.D6_PWM, Buzzer.pin2
  N16: Arduino_Uno.D7, LCD.DB4

custom parts:
  HC-12 Antenna: Antenna for HC-12 433Mhz Module
  HC-12 Module: HC-12 433Mhz Module
